// Logisim project 实验2-CSXJ1901-U201912703-时深奥.circ as structural Verilog: 10 circuits, main circuit 先行进位的四位二进制并行加法器
module \先行进位的四位二进制并行加法器  (
  input  C0,
  input  A0,
  input  B0,
  input  A1,
  input  B1,
  input  A2,
  input  B2,
  input  A3,
  input  B3,
  output S0,
  output S1,
  output S2,
  output S3,
  output C4
);

  wire and_1_out, and_2_out, and_3_out, and_4_out, and_5_out, and_6_out, and_7_out, and_8_out, and_9_out,
       and_10_out, and_11_out, and_12_out, and_13_out, and_14_out, or_1_out, or_2_out, or_3_out, xor_1_out,
       xor_2_out, xor_3_out, xor_4_out;

  xor xor_1 (xor_1_out, A0, B0);
  and and_1 (and_1_out, A0, B0);
  xor xor_2 (xor_2_out, A1, B1);
  and and_2 (and_2_out, A1, B1);
  xor xor_3 (xor_3_out, A2, B2);
  and and_3 (and_3_out, A2, B2);
  xor xor_4 (xor_4_out, A3, B3);
  and and_4 (and_4_out, A3, B3);
  and and_5 (and_5_out, C0, xor_1_out);
  and and_6 (and_6_out, and_1_out, xor_2_out);
  and and_7 (and_7_out, xor_2_out, xor_1_out, C0);
  and and_8 (and_8_out, and_2_out, xor_3_out);
  and and_9 (and_9_out, xor_3_out, xor_2_out, and_1_out);
  and and_10 (and_10_out, xor_3_out, xor_2_out, xor_1_out, C0);
  and and_11 (and_11_out, and_3_out, xor_4_out);
  and and_12 (and_12_out, and_2_out, xor_3_out, xor_4_out);
  and and_13 (and_13_out, xor_4_out, xor_3_out, xor_2_out, and_1_out);
  and and_14 (and_14_out, xor_4_out, xor_3_out, xor_2_out, xor_1_out, C0);
  or or_1 (or_1_out, and_5_out, and_1_out);
  or or_2 (or_2_out, and_6_out, and_7_out, and_2_out);
  or or_3 (or_3_out, and_8_out, and_9_out, and_10_out, and_3_out);
  or or_4 (C4, and_11_out, and_12_out, and_13_out, and_14_out, and_4_out);
  xor xor_5 (S0, C0, xor_1_out);
  xor xor_6 (S1, or_1_out, xor_2_out);
  xor xor_7 (S2, or_2_out, xor_3_out);
  xor xor_8 (S3, or_3_out, xor_4_out);

  // Notes on the sheet:
  //   P1
  //   G1
  //   P2
  //   G2
  //   P3
  //   G3
  //   P4
  //   G4
  //   C1
  //   C2
  //   C3
endmodule

module \四位二进制可逆计数器  (
  input  CPD,
  input  CPU,
  input  A,
  input  CLR,
  input  B,
  input  nLD,
  input  C,
  input  D,
  output QA,
  output QB,
  output QC,
  output QD
);

  wire and_1_out, and_2_out, and_3_out, and_4_out, and_5_out, and_6_out, and_7_out, and_8_out, and_9_out,
       and_10_out, and_11_out, and_12_out, and_13_out, and_14_out, D1_qn, D2_qn, D3_qn, D4_qn, not_1_out,
       not_2_out, not_3_out, not_4_out, not_5_out, or_1_out, or_2_out, or_3_out, or_4_out, or_5_out,
       or_6_out, or_7_out, or_8_out;

  or or_1 (or_1_out, CPD, CPU);
  and and_1 (and_1_out, D1_qn, CPD);
  and and_2 (and_2_out, QA, CPU);
  and and_3 (and_3_out, D1_qn, D2_qn, CPD);
  and and_4 (and_4_out, QA, QB, CPU);
  and and_5 (and_5_out, D1_qn, D2_qn, D3_qn, CPD);
  and and_6 (and_6_out, QA, QB, QC, CPU);
  or or_2 (or_2_out, and_1_out, and_2_out);
  or or_3 (or_3_out, and_3_out, and_4_out);
  or or_4 (or_4_out, and_5_out, and_6_out);
  D_Flip_Flop #(.trigger("falling"), .Pre_Clr_Positions("LEGACY"), .NegatePresetClear("false"), .enable("true"), .NewFFLayout("false")) D1 (
    .clk(or_1_out), .D(D1_qn), .Q(QA), .Qn(D1_qn), .preset(and_7_out), .en(nLD), .reset(or_5_out));
  or or_5 (or_5_out, and_8_out, CLR);
  D_Flip_Flop #(.trigger("falling"), .Pre_Clr_Positions("LEGACY"), .NegatePresetClear("false"), .enable("true"), .NewFFLayout("false")) D2 (
    .clk(or_2_out), .D(D2_qn), .Q(QB), .Qn(D2_qn), .preset(and_9_out), .en(nLD), .reset(or_6_out));
  or or_6 (or_6_out, and_10_out, CLR);
  D_Flip_Flop #(.trigger("falling"), .Pre_Clr_Positions("LEGACY"), .NegatePresetClear("false"), .enable("true"), .NewFFLayout("false")) D3 (
    .clk(or_3_out), .D(D3_qn), .Q(QC), .Qn(D3_qn), .preset(and_11_out), .en(nLD), .reset(or_7_out));
  or or_7 (or_7_out, and_12_out, CLR);
  D_Flip_Flop #(.trigger("falling"), .Pre_Clr_Positions("LEGACY"), .NegatePresetClear("false"), .enable("true"), .NewFFLayout("false")) D4 (
    .clk(or_4_out), .D(D4_qn), .Q(QD), .Qn(D4_qn), .preset(and_13_out), .en(nLD), .reset(or_8_out));
  or or_8 (or_8_out, and_14_out, CLR);
  and and_7 (and_7_out, not_5_out, A);
  and and_8 (and_8_out, not_1_out, not_5_out);
  and and_9 (and_9_out, B, not_5_out);
  and and_10 (and_10_out, not_2_out, not_5_out);
  and and_11 (and_11_out, C, not_5_out);
  and and_12 (and_12_out, not_3_out, not_5_out);
  and and_13 (and_13_out, D, not_5_out);
  and and_14 (and_14_out, not_4_out, not_5_out);
  not not_1 (not_1_out, A);
  not not_2 (not_2_out, B);
  not not_3 (not_3_out, C);
  not not_4 (not_4_out, D);
  not not_5 (not_5_out, nLD);
endmodule

module \四位二进制可逆计数器测试电路  (
  input  CPU,
  input  CLR,
  input  CPD,
  input  D,
  input  C,
  input  B,
  input  A,
  input  nLD,
  output QD,
  output QC,
  output QB,
  output QA
);

  \四位二进制可逆计数器  \u_四位二进制可逆计数器_1  (
    .QA(QA), .A(A), .CLR(CLR), .QB(QB), .B(B), .nLD(nLD), .QC(QC), .C(C), .QD(QD), .D(D), .CPD(CPD), .CPU(CPU));
endmodule

module \二进制转8421BCD码电路  (
  input  A3,
  input  A2,
  input  A1,
  input  A0,
  output S4,
  output S7,
  output S6,
  output S5,
  output S3,
  output S2,
  output S1,
  output S0
);

  wire or_1_out;

  or or_1 (or_1_out, A2, A1);
  and and_1 (S4, or_1_out, A3);
  \先行进位的四位二进制并行加法器  \u_先行进位的四位二进制并行加法器_1  (
    .C0(1'b0), .A0(A0), .B0(1'b0), .A1(A1), .B1(S4), .A2(A2), .B2(S4), .A3(A3), .B3(1'b0), .S0(S0), .S1(S1),
    .S2(S2), .S3(S3));  // open: C4

  assign S5 = 1'b0;
  assign S6 = 1'b0;
  assign S7 = 1'b0;
endmodule

module \二进制转8421BCD码电路测试电路  (
  input  A3,
  input  A2,
  input  A1,
  input  A0,
  output S7,
  output S6,
  output S5,
  output S4,
  output S3,
  output S2,
  output S1,
  output S0
);

  \二进制转8421BCD码电路  \u_二进制转8421bcd码电路_1  (
    .S7(S7), .S6(S6), .S5(S5), .S3(S3), .S2(S2), .S1(S1), .S0(S0), .S4(S4), .A0(A0), .A1(A1), .A2(A2), .A3(A3));
endmodule

module \显示电路  (
  input  A3,
  input  A2,
  input  A1,
  input  A0,
  output a,
  output b,
  output c,
  output d,
  output e,
  output f,
  output g
);

  wire and_1_out, and_2_out, and_3_out, and_4_out, and_5_out, and_6_out, and_7_out, and_8_out, and_9_out,
       and_10_out, and_11_out, and_12_out, and_13_out, and_14_out, and_15_out, and_16_out, and_17_out,
       and_18_out, and_19_out, and_20_out, and_21_out, and_22_out, and_23_out, and_24_out, and_25_out,
       not_1_out, not_2_out, not_3_out, not_4_out, not_5_out, not_6_out, not_7_out, not_8_out, not_9_out,
       not_10_out, not_11_out, not_12_out, not_13_out, not_14_out, not_15_out, not_16_out, not_17_out,
       not_18_out, not_19_out, not_20_out, not_21_out, not_22_out, not_23_out, not_24_out, not_25_out,
       not_26_out, not_27_out, not_28_out, not_29_out, not_30_out, not_31_out, not_32_out, not_33_out,
       not_34_out, not_35_out, not_36_out, not_37_out, not_38_out, not_39_out, not_40_out, not_41_out,
       not_42_out, not_43_out, not_44_out, not_45_out, not_46_out, not_47_out, not_48_out, not_49_out,
       not_50_out, not_51_out;

  not not_1 (not_1_out, A3);
  and and_1 (and_1_out, not_1_out, not_2_out, not_3_out);
  not not_2 (not_2_out, A2);
  not not_3 (not_3_out, A0);
  not not_4 (not_4_out, A3);
  not not_5 (not_5_out, A2);
  and and_2 (and_2_out, not_4_out, not_5_out, A1);
  not not_6 (not_6_out, A3);
  and and_3 (and_3_out, not_6_out, A2, A0);
  and and_4 (and_4_out, A3, not_7_out, not_8_out);
  not not_7 (not_7_out, A2);
  not not_8 (not_8_out, A1);
  not not_9 (not_9_out, A3);
  and and_5 (and_5_out, not_9_out, not_10_out);
  not not_10 (not_10_out, A2);
  not not_11 (not_11_out, A3);
  and and_6 (and_6_out, not_11_out, not_12_out, not_13_out);
  not not_12 (not_12_out, A1);
  not not_13 (not_13_out, A0);
  not not_14 (not_14_out, A2);
  and and_7 (and_7_out, not_14_out, not_15_out);
  not not_15 (not_15_out, A1);
  not not_16 (not_16_out, A3);
  and and_8 (and_8_out, not_16_out, A1, A0);
  not not_17 (not_17_out, A2);
  and and_9 (and_9_out, not_17_out, not_18_out);
  not not_18 (not_18_out, A1);
  not not_19 (not_19_out, A3);
  and and_10 (and_10_out, not_19_out, A0);
  not not_20 (not_20_out, A3);
  and and_11 (and_11_out, not_20_out, A2);
  not not_21 (not_21_out, A2);
  not not_22 (not_22_out, A1);
  not not_23 (not_23_out, A0);
  not not_24 (not_24_out, A3);
  not not_25 (not_25_out, A2);
  not not_26 (not_26_out, A3);
  not not_27 (not_27_out, A0);
  not not_28 (not_28_out, A3);
  not not_29 (not_29_out, A1);
  not not_30 (not_30_out, A2);
  not not_31 (not_31_out, A1);
  and and_12 (and_12_out, not_30_out, not_31_out, not_32_out);
  not not_32 (not_32_out, A0);
  not not_33 (not_33_out, A3);
  and and_13 (and_13_out, not_33_out, A1, not_34_out);
  not not_34 (not_34_out, A0);
  not not_35 (not_35_out, A3);
  not not_36 (not_36_out, A1);
  and and_14 (and_14_out, not_35_out, not_36_out, not_37_out);
  not not_37 (not_37_out, A0);
  not not_38 (not_38_out, A3);
  and and_15 (and_15_out, not_38_out, A2, not_39_out);
  not not_39 (not_39_out, A1);
  not not_40 (not_40_out, A3);
  and and_16 (and_16_out, not_40_out, A2, not_41_out);
  not not_41 (not_41_out, A0);
  and and_17 (and_17_out, A3, not_42_out, not_43_out);
  not not_42 (not_42_out, A2);
  not not_43 (not_43_out, A1);
  not not_44 (not_44_out, A3);
  not not_45 (not_45_out, A2);
  and and_18 (and_18_out, not_44_out, not_45_out, A1);
  not not_46 (not_46_out, A3);
  and and_19 (and_19_out, not_46_out, A2, not_47_out);
  not not_47 (not_47_out, A1);
  not not_48 (not_48_out, A3);
  and and_20 (and_20_out, not_48_out, A2, not_49_out);
  not not_49 (not_49_out, A0);
  and and_21 (and_21_out, A3, not_50_out, not_51_out);
  not not_50 (not_50_out, A2);
  not not_51 (not_51_out, A1);
  or or_1 (a, and_1_out, and_2_out, and_3_out, and_4_out);
  or or_2 (b, and_5_out, and_6_out, and_7_out, and_8_out);
  or or_3 (c, and_9_out, and_10_out, and_11_out);
  and and_22 (and_22_out, not_21_out, not_22_out, not_23_out);
  and and_23 (and_23_out, not_24_out, not_25_out, A1);
  and and_24 (and_24_out, not_26_out, A1, not_27_out);
  and and_25 (and_25_out, not_28_out, A2, not_29_out, A0);
  or or_4 (e, and_12_out, and_13_out);
  or or_5 (f, and_14_out, and_15_out, and_16_out, and_17_out);
  or or_6 (g, and_18_out, and_19_out, and_20_out, and_21_out);
  or or_7 (d, and_22_out, and_23_out, and_24_out, and_25_out);
endmodule

module \显示电路测试电路  (
  input  A3,
  input  A2,
  input  A1,
  input  A0
);

  wire \二进制转8421bcd码电路_1_s0 , \二进制转8421bcd码电路_1_s1 , \二进制转8421bcd码电路_1_s2 , \二进制转8421bcd码电路_1_s3 ,
       \二进制转8421bcd码电路_1_s4 , \二进制转8421bcd码电路_1_s5 , \二进制转8421bcd码电路_1_s6 , \二进制转8421bcd码电路_1_s7 ,
       \显示电路_1_a , \显示电路_1_b , \显示电路_1_c , \显示电路_1_d , \显示电路_1_e , \显示电路_1_f , \显示电路_1_g , \显示电路_2_a ,
       \显示电路_2_b , \显示电路_2_c , \显示电路_2_d , \显示电路_2_e , \显示电路_2_f , \显示电路_2_g ;

  _7_Segment_Display #(.active("true")) u_7_segment_display_1 (
    .g(\显示电路_1_g ), .f(\显示电路_1_f ), .a(\显示电路_1_a ), .b(\显示电路_1_b ), .e(\显示电路_1_e ), .d(\显示电路_1_d ),
    .c(\显示电路_1_c ));  // open: dp
  \显示电路  \u_显示电路_1  (
    .A3(\二进制转8421bcd码电路_1_s7 ), .A2(\二进制转8421bcd码电路_1_s6 ), .A1(\二进制转8421bcd码电路_1_s5 ), .a(\显示电路_1_a ),
    .A0(\二进制转8421bcd码电路_1_s4 ), .b(\显示电路_1_b ), .c(\显示电路_1_c ), .d(\显示电路_1_d ), .e(\显示电路_1_e ),
    .f(\显示电路_1_f ), .g(\显示电路_1_g ));
  _7_Segment_Display #(.active("true")) u_7_segment_display_2 (
    .g(\显示电路_2_g ), .f(\显示电路_2_f ), .a(\显示电路_2_a ), .b(\显示电路_2_b ), .e(\显示电路_2_e ), .d(\显示电路_2_d ),
    .c(\显示电路_2_c ));  // open: dp
  \二进制转8421BCD码电路  \u_二进制转8421bcd码电路_1  (
    .S7(\二进制转8421bcd码电路_1_s7 ), .S6(\二进制转8421bcd码电路_1_s6 ), .S5(\二进制转8421bcd码电路_1_s5 ),
    .S3(\二进制转8421bcd码电路_1_s3 ), .S2(\二进制转8421bcd码电路_1_s2 ), .S1(\二进制转8421bcd码电路_1_s1 ),
    .S0(\二进制转8421bcd码电路_1_s0 ), .S4(\二进制转8421bcd码电路_1_s4 ), .A0(A0), .A1(A1), .A2(A2), .A3(A3));
  \显示电路  \u_显示电路_2  (
    .A3(\二进制转8421bcd码电路_1_s3 ), .A2(\二进制转8421bcd码电路_1_s2 ), .A1(\二进制转8421bcd码电路_1_s1 ), .a(\显示电路_2_a ),
    .A0(\二进制转8421bcd码电路_1_s0 ), .b(\显示电路_2_b ), .c(\显示电路_2_c ), .d(\显示电路_2_d ), .e(\显示电路_2_e ),
    .f(\显示电路_2_f ), .g(\显示电路_2_g ));
endmodule

module \报警电路  (
  input  CLR,
  input  D,
  input  C,
  input  B,
  input  A,
  input  nLD
);

  wire and_1_out, and_2_out, and_3_out, and_4_out, CPD_out, CPU_out, not_1_out, or_1_out, \四位二进制可逆计数器_1_qa ,
       \四位二进制可逆计数器_1_qb , \四位二进制可逆计数器_1_qc , \四位二进制可逆计数器_1_qd ;

  Button CPD (.out(CPD_out));
  Button CPU (.out(CPU_out));
  not not_1 (not_1_out, and_3_out);
  and and_1 (and_1_out, or_1_out, CPD_out);
  and and_2 (and_2_out, not_1_out, CPU_out);
  or or_1 (or_1_out, \四位二进制可逆计数器_1_qd , \四位二进制可逆计数器_1_qc , \四位二进制可逆计数器_1_qb , \四位二进制可逆计数器_1_qa );
  and and_3 (and_3_out, \四位二进制可逆计数器_1_qa , \四位二进制可逆计数器_1_qb , \四位二进制可逆计数器_1_qc , \四位二进制可逆计数器_1_qd );
  \四位二进制可逆计数器  \u_四位二进制可逆计数器_1  (
    .QA(\四位二进制可逆计数器_1_qa ), .A(A), .CLR(CLR), .QB(\四位二进制可逆计数器_1_qb ), .B(B), .nLD(nLD),
    .QC(\四位二进制可逆计数器_1_qc ), .C(C), .QD(\四位二进制可逆计数器_1_qd ), .D(D), .CPD(and_1_out), .CPU(and_2_out));
  LED #(.active("true")) led_1 (.in(and_4_out));
  and and_4 (and_4_out, and_3_out, CPU_out);

  // Notes on the sheet:
  //   满员
endmodule

module \小型实验室门禁系统  (
  input  CPU,
  input  CLR,
  input  CPD,
  output a1,
  output c1,
  output e1,
  output g1,
  output a0,
  output c0,
  output e0,
  output g0,
  output b1,
  output d1,
  output f1,
  output b0,
  output d0,
  output f0,
  output warning
);

  wire and_1_out, and_2_out, and_4_out, not_1_out, or_1_out, \二进制转8421bcd码电路_1_s0 , \二进制转8421bcd码电路_1_s1 ,
       \二进制转8421bcd码电路_1_s2 , \二进制转8421bcd码电路_1_s3 , \二进制转8421bcd码电路_1_s4 , \二进制转8421bcd码电路_1_s5 ,
       \二进制转8421bcd码电路_1_s6 , \二进制转8421bcd码电路_1_s7 , \四位二进制可逆计数器_1_qa , \四位二进制可逆计数器_1_qb , \四位二进制可逆计数器_1_qc ,
       \四位二进制可逆计数器_1_qd ;

  \显示电路  \u_显示电路_1  (
    .A3(\二进制转8421bcd码电路_1_s7 ), .A2(\二进制转8421bcd码电路_1_s6 ), .A1(\二进制转8421bcd码电路_1_s5 ), .a(a1),
    .A0(\二进制转8421bcd码电路_1_s4 ), .b(b1), .c(c1), .d(d1), .e(e1), .f(f1), .g(g1));
  \二进制转8421BCD码电路  \u_二进制转8421bcd码电路_1  (
    .S7(\二进制转8421bcd码电路_1_s7 ), .S6(\二进制转8421bcd码电路_1_s6 ), .S5(\二进制转8421bcd码电路_1_s5 ),
    .S3(\二进制转8421bcd码电路_1_s3 ), .S2(\二进制转8421bcd码电路_1_s2 ), .S1(\二进制转8421bcd码电路_1_s1 ),
    .S0(\二进制转8421bcd码电路_1_s0 ), .S4(\二进制转8421bcd码电路_1_s4 ), .A0(\四位二进制可逆计数器_1_qa ), .A1(\四位二进制可逆计数器_1_qb ),
    .A2(\四位二进制可逆计数器_1_qc ), .A3(\四位二进制可逆计数器_1_qd ));
  \显示电路  \u_显示电路_2  (
    .A3(\二进制转8421bcd码电路_1_s3 ), .A2(\二进制转8421bcd码电路_1_s2 ), .A1(\二进制转8421bcd码电路_1_s1 ), .a(a0),
    .A0(\二进制转8421bcd码电路_1_s0 ), .b(b0), .c(c0), .d(d0), .e(e0), .f(f0), .g(g0));
  not not_1 (not_1_out, and_4_out);
  and and_1 (and_1_out, or_1_out, CPD);
  and and_2 (and_2_out, not_1_out, CPU);
  or or_1 (or_1_out, \四位二进制可逆计数器_1_qd , \四位二进制可逆计数器_1_qc , \四位二进制可逆计数器_1_qb , \四位二进制可逆计数器_1_qa );
  \四位二进制可逆计数器  \u_四位二进制可逆计数器_1  (
    .QA(\四位二进制可逆计数器_1_qa ), .A(1'b0), .CLR(CLR), .QB(\四位二进制可逆计数器_1_qb ), .B(1'b0), .nLD(1'b1),
    .QC(\四位二进制可逆计数器_1_qc ), .C(1'b0), .QD(\四位二进制可逆计数器_1_qd ), .D(1'b0), .CPD(and_1_out), .CPU(and_2_out));
  and and_3 (warning, and_4_out, CPU);
  and and_4 (and_4_out, \四位二进制可逆计数器_1_qa , \四位二进制可逆计数器_1_qb , \四位二进制可逆计数器_1_qc , \四位二进制可逆计数器_1_qd );

  // Notes on the sheet:
  //   满员
endmodule

module \小型门禁系统测试电路  (
  input  CPU,
  input  CLR,
  input  CPD
);

  wire \小型实验室门禁系统_1_p4 , \小型实验室门禁系统_1_p5 , \小型实验室门禁系统_1_p6 , \小型实验室门禁系统_1_p7 , \小型实验室门禁系统_1_p8 ,
       \小型实验室门禁系统_1_p9 , \小型实验室门禁系统_1_p10 , \小型实验室门禁系统_1_p11 , \小型实验室门禁系统_1_p12 , \小型实验室门禁系统_1_p13 ,
       \小型实验室门禁系统_1_p14 , \小型实验室门禁系统_1_p15 , \小型实验室门禁系统_1_p16 , \小型实验室门禁系统_1_p17 , \小型实验室门禁系统_1_p18 ;

  _7_Segment_Display #(.active("true")) u_7_segment_display_1 (
    .g(\小型实验室门禁系统_1_p10 ), .f(\小型实验室门禁系统_1_p9 ), .a(\小型实验室门禁系统_1_p4 ), .b(\小型实验室门禁系统_1_p5 ),
    .e(\小型实验室门禁系统_1_p8 ), .d(\小型实验室门禁系统_1_p7 ), .c(\小型实验室门禁系统_1_p6 ));  // open: dp
  _7_Segment_Display #(.active("true")) u_7_segment_display_2 (
    .g(\小型实验室门禁系统_1_p17 ), .f(\小型实验室门禁系统_1_p16 ), .a(\小型实验室门禁系统_1_p11 ), .b(\小型实验室门禁系统_1_p12 ),
    .e(\小型实验室门禁系统_1_p15 ), .d(\小型实验室门禁系统_1_p14 ), .c(\小型实验室门禁系统_1_p13 ));  // open: dp
  // 小型实验室门禁系统 小型实验室门禁系统_1: pin names not known; wires that end beside it: CPU, CLR, CPD, \小型实验室门禁系统_1_p4 , \小型实验室门禁系统_1_p5 , \小型实验室门禁系统_1_p6 , \小型实验室门禁系统_1_p7 , \小型实验室门禁系统_1_p8 , \小型实验室门禁系统_1_p9 , \小型实验室门禁系统_1_p10 , \小型实验室门禁系统_1_p11 , \小型实验室门禁系统_1_p12 , \小型实验室门禁系统_1_p13 , \小型实验室门禁系统_1_p14 , \小型实验室门禁系统_1_p15 , \小型实验室门禁系统_1_p16 , \小型实验室门禁系统_1_p17 , \小型实验室门禁系统_1_p18 
  LED #(.active("true")) led_1 (.in(\小型实验室门禁系统_1_p18 ));
endmodule
