// Logisim project 实验3-CSXJ1901-U201912703-时深奥.circ as structural Verilog: 6 circuits, main circuit 四位乘法器
module \四位乘法器  (
  input  [3:0] a_3_0,
  input  [3:0] b_3_0,
  output [7:0] p_7_0
);

  wire [7:0] adder_1_out, adder_2_out, adder_3_out, adder_4_out, bit_extender_1_out, multiplexer_1_out,
       multiplexer_2_out, multiplexer_3_out, shifter_1_out, shifter_2_out, shifter_3_out;

  assign bit_extender_1_out = {{4{1'b0}}, b_3_0};  // Bit_Extender bit_extender_1
  Adder #(.width(8)) adder_1 (.a({8{1'b0}}), .b(bit_extender_1_out), .out(adder_1_out));  // open: cin, cout
  Multiplexer #(.select(1), .width(8), .disabled("Z"), .enable("false")) multiplexer_1 (
    .in0({8{1'b0}}), .in1(adder_1_out), .out(multiplexer_1_out), .sel(a_3_0[0]));
  Shifter #(.width(8), .shift("ll")) shifter_1 (.in(bit_extender_1_out), .\dist (3'b001), .out(shifter_1_out));
  Adder #(.width(8)) adder_2 (.a(multiplexer_1_out), .b(shifter_1_out), .out(adder_2_out));  // open: cin, cout
  Multiplexer #(.select(1), .width(8), .disabled("Z"), .enable("false")) multiplexer_2 (
    .in0(multiplexer_1_out), .in1(adder_2_out), .out(multiplexer_2_out), .sel(a_3_0[1]));
  Shifter #(.width(8), .shift("ll")) shifter_2 (.in(shifter_1_out), .\dist (3'b001), .out(shifter_2_out));
  Multiplexer #(.select(1), .width(8), .disabled("Z"), .enable("false")) multiplexer_3 (
    .in0(multiplexer_2_out), .in1(adder_3_out), .out(multiplexer_3_out), .sel(a_3_0[2]));
  Adder #(.width(8)) adder_3 (.a(multiplexer_2_out), .b(shifter_2_out), .out(adder_3_out));  // open: cin, cout
  Shifter #(.width(8), .shift("ll")) shifter_3 (.in(shifter_2_out), .\dist (3'b001), .out(shifter_3_out));
  Adder #(.width(8)) adder_4 (.a(multiplexer_3_out), .b(shifter_3_out), .out(adder_4_out));  // open: cin, cout
  Multiplexer #(.select(1), .width(8), .disabled("Z"), .enable("false")) multiplexer_4 (
    .in0(multiplexer_3_out), .in1(adder_4_out), .out(p_7_0), .sel(a_3_0[3]));
endmodule

module \四位乘法器测试电路  (
  input  [3:0] a_3_0,
  input  [3:0] b_3_0,
  output [7:0] p_7_0,
  output [7:0] out_4,
  output [7:0] p_7_0_2
);

  wire [3:0] multiplier_1_out;

  Multiplier #(.width(4)) multiplier_1 (.a(a_3_0), .b(b_3_0), .out(multiplier_1_out));  // open: cin, cout
  assign p_7_0_2 = {{4{1'b0}}, multiplier_1_out};  // Bit_Extender bit_extender_1
  \四位乘法器  \u_四位乘法器_1  (.a_3_0(a_3_0), .b_3_0(b_3_0), .p_7_0(p_7_0));
  assign out_4 = p_7_0 ^ p_7_0_2;  // XOR_Gate xor_1, 8 bits wide
endmodule

module \_32X4乘法器  (
  input  [3:0] a_3_0,
  input  [31:0] b_31_0,
  output [31:0] p_63_32,
  output [31:0] p_31_0
);

  wire adder_2_cout, adder_4_cout, adder_6_cout, adder_10_cout, and_1_out, and_2_out, and_3_out, and_4_out;
  wire [3:0] adder_1_out, adder_3_out, adder_5_out, multiplexer_1_out, multiplexer_3_out, multiplexer_5_out,
       shifter_1_out, shifter_2_out, shifter_5_out;
  wire [31:0] adder_2_out, adder_4_out, adder_6_out, adder_7_out, adder_9_out, adder_10_out, adder_11_out,
       bit_extender_1_out, bit_extender_2_out, bit_extender_3_out, bit_extender_4_out, bit_extender_5_out,
       multiplexer_2_out, multiplexer_4_out, multiplexer_6_out, shifter_3_out, shifter_4_out, shifter_6_out;

  Adder #(.width(4)) adder_1 (.a(4'b0000), .b(shifter_1_out), .out(adder_1_out));  // open: cin, cout
  Shifter #(.width(4), .shift("lr")) shifter_1 (.in(b_31_0[31:28]), .\dist (2'b01), .out(shifter_1_out));
  Adder #(.width(32)) adder_2 (.a({32{1'b0}}), .b(b_31_0), .out(adder_2_out), .cout(adder_2_cout));  // open: cin
  Multiplexer #(.select(1), .width(4), .disabled("Z"), .enable("false")) multiplexer_1 (
    .in0(4'b0000), .in1(adder_1_out), .out(multiplexer_1_out), .sel(a_3_0[3]));
  Shifter #(.width(4), .shift("lr")) shifter_2 (.in(shifter_1_out), .\dist (2'b01), .out(shifter_2_out));
  Multiplexer #(.select(1), .width(32), .disabled("Z"), .enable("false")) multiplexer_2 (
    .in0({32{1'b0}}), .in1(adder_2_out), .out(multiplexer_2_out), .sel(a_3_0[0]));
  and and_1 (and_1_out, a_3_0[0], adder_2_cout);
  Shifter #(.width(32), .shift("ll")) shifter_3 (.in(b_31_0), .\dist (5'b00001), .out(shifter_3_out));
  Adder #(.width(4)) adder_3 (.a(multiplexer_1_out), .b(shifter_2_out), .out(adder_3_out));  // open: cin, cout
  assign bit_extender_1_out = {{31{1'b0}}, and_1_out};  // Bit_Extender bit_extender_1
  Adder #(.width(32)) adder_4 (
    .a(multiplexer_2_out), .b(shifter_3_out), .out(adder_4_out), .cout(adder_4_cout));  // open: cin
  Multiplexer #(.select(1), .width(4), .disabled("Z"), .enable("false")) multiplexer_3 (
    .in0(multiplexer_1_out), .in1(adder_3_out), .out(multiplexer_3_out), .sel(a_3_0[2]));
  Adder #(.width(4)) adder_5 (.a(multiplexer_3_out), .b(shifter_5_out), .out(adder_5_out));  // open: cin, cout
  Multiplexer #(.select(1), .width(32), .disabled("Z"), .enable("false")) multiplexer_4 (
    .in0(multiplexer_2_out), .in1(adder_4_out), .out(multiplexer_4_out), .sel(a_3_0[1]));
  and and_2 (and_2_out, a_3_0[1], adder_4_cout);
  Shifter #(.width(32), .shift("ll")) shifter_4 (.in(shifter_3_out), .\dist (5'b00001), .out(shifter_4_out));
  Multiplexer #(.select(1), .width(4), .disabled("Z"), .enable("false")) multiplexer_5 (
    .in0(multiplexer_3_out), .in1(adder_5_out), .out(multiplexer_5_out), .sel(a_3_0[1]));
  Shifter #(.width(4), .shift("lr")) shifter_5 (.in(shifter_2_out), .\dist (2'b01), .out(shifter_5_out));
  assign bit_extender_2_out = {{31{1'b0}}, and_2_out};  // Bit_Extender bit_extender_2
  Adder #(.width(32)) adder_6 (
    .a(multiplexer_4_out), .b(shifter_4_out), .out(adder_6_out), .cout(adder_6_cout));  // open: cin
  assign bit_extender_3_out = {{28{1'b0}}, multiplexer_5_out};  // Bit_Extender bit_extender_3
  Adder #(.width(32)) adder_7 (.a(adder_9_out), .b(adder_11_out), .out(adder_7_out));  // open: cin, cout
  Multiplexer #(.select(1), .width(32), .disabled("Z"), .enable("false")) multiplexer_6 (
    .in0(multiplexer_4_out), .in1(adder_6_out), .out(multiplexer_6_out), .sel(a_3_0[2]));
  and and_3 (and_3_out, a_3_0[2], adder_6_cout);
  Shifter #(.width(32), .shift("ll")) shifter_6 (.in(shifter_4_out), .\dist (5'b00001), .out(shifter_6_out));
  Adder #(.width(32)) adder_8 (.a(bit_extender_3_out), .b(adder_7_out), .out(p_63_32));  // open: cin, cout
  Adder #(.width(32)) adder_9 (.a(bit_extender_1_out), .b(bit_extender_2_out), .out(adder_9_out));  // open: cin, cout
  assign bit_extender_4_out = {{31{1'b0}}, and_3_out};  // Bit_Extender bit_extender_4
  Multiplexer #(.select(1), .width(32), .disabled("Z"), .enable("false")) multiplexer_7 (
    .in0(multiplexer_6_out), .in1(adder_10_out), .out(p_31_0), .sel(a_3_0[3]));
  Adder #(.width(32)) adder_10 (
    .a(multiplexer_6_out), .b(shifter_6_out), .out(adder_10_out), .cout(adder_10_cout));  // open: cin
  Adder #(.width(32)) adder_11 (.a(bit_extender_4_out), .b(bit_extender_5_out), .out(adder_11_out));  // open: cin, cout
  and and_4 (and_4_out, a_3_0[3], adder_10_cout);
  assign bit_extender_5_out = {{31{1'b0}}, and_4_out};  // Bit_Extender bit_extender_5
endmodule

module \_32X4乘法器测试电路  (
  input  [3:0] a_3_0,
  input  [31:0] b_31_0,
  output [31:0] p_63_32,
  output [31:0] p_31_0,
  output [31:0] out_5,
  output [31:0] p_31_0_2,
  output [31:0] p_63_32_2
);

  wire [31:0] bit_extender_1_out;

  assign bit_extender_1_out = {{28{1'b0}}, a_3_0};  // Bit_Extender bit_extender_1
  \_32X4乘法器  \u_32x4乘法器_1  (.a_3_0(a_3_0), .b_31_0(b_31_0), .p_31_0(p_31_0), .p_63_32(p_63_32));
  Multiplier #(.width(32)) multiplier_1 (
    .a(bit_extender_1_out), .b(b_31_0), .out(p_31_0_2), .cout(p_63_32_2));  // open: cin
  assign out_5 = p_31_0 ^ p_31_0_2;  // XOR_Gate xor_1, 32 bits wide
endmodule

module \_32X32乘法器  (
  input  [31:0] in_1,
  input  [31:0] in_2,
  output [31:0] p_63_32,
  output [31:0] p_31_0
);

  wire adder_3_cout, adder_6_cout, adder_10_cout, adder_14_cout, adder_17_cout, adder_22_cout, adder_26_cout;
  wire [31:0] adder_1_out, adder_2_out, adder_3_out, adder_4_out, adder_5_out, adder_6_out, adder_7_out,
       adder_8_out, adder_9_out, adder_10_out, adder_11_out, adder_12_out, adder_13_out, adder_14_out,
       adder_15_out, adder_16_out, adder_17_out, adder_18_out, adder_19_out, adder_20_out, adder_21_out,
       adder_22_out, adder_23_out, adder_24_out, adder_25_out, adder_27_out, bit_extender_1_out,
       bit_extender_2_out, bit_extender_3_out, bit_extender_4_out, bit_extender_5_out, bit_extender_6_out,
       bit_extender_7_out, bit_extender_8_out, bit_extender_9_out, bit_extender_10_out, bit_extender_11_out,
       bit_extender_12_out, bit_extender_13_out, bit_extender_14_out, \n32x4乘法器_1_p_31_0 ,
       \n32x4乘法器_1_p_63_32 , \n32x4乘法器_2_p_31_0 , \n32x4乘法器_2_p_63_32 , \n32x4乘法器_3_p_31_0 ,
       \n32x4乘法器_3_p_63_32 , \n32x4乘法器_4_p_31_0 , \n32x4乘法器_4_p_63_32 , \n32x4乘法器_5_p_31_0 ,
       \n32x4乘法器_5_p_63_32 , \n32x4乘法器_6_p_31_0 , \n32x4乘法器_6_p_63_32 , \n32x4乘法器_7_p_31_0 ,
       \n32x4乘法器_7_p_63_32 , \n32x4乘法器_8_p_31_0 , \n32x4乘法器_8_p_63_32 , shifter_1_out, shifter_2_out,
       shifter_3_out, shifter_4_out, shifter_5_out, shifter_6_out, shifter_7_out, shifter_8_out,
       shifter_9_out, shifter_10_out, shifter_11_out, shifter_12_out, shifter_13_out, shifter_14_out;

  \_32X4乘法器  \u_32x4乘法器_1  (
    .a_3_0(in_1[3:0]), .b_31_0(in_2), .p_31_0(\n32x4乘法器_1_p_31_0 ), .p_63_32(\n32x4乘法器_1_p_63_32 ));
  Shifter #(.width(32), .shift("ll")) shifter_1 (.in(\n32x4乘法器_2_p_63_32 ), .\dist (5'b00100), .out(shifter_1_out));
  \_32X4乘法器  \u_32x4乘法器_2  (
    .a_3_0(in_1[7:4]), .b_31_0(in_2), .p_31_0(\n32x4乘法器_2_p_31_0 ), .p_63_32(\n32x4乘法器_2_p_63_32 ));
  Adder #(.width(32)) adder_1 (.a(shifter_1_out), .b(bit_extender_1_out), .out(adder_1_out));  // open: cin, cout
  assign bit_extender_1_out = {{28{1'b0}}, \n32x4乘法器_2_p_31_0 [31:28]};  // Bit_Extender bit_extender_1
  Shifter #(.width(32), .shift("ll")) shifter_2 (.in(\n32x4乘法器_2_p_31_0 ), .\dist (5'b00100), .out(shifter_2_out));
  Adder #(.width(32)) adder_2 (.a(\n32x4乘法器_1_p_63_32 ), .b(adder_1_out), .out(adder_2_out));  // open: cin, cout
  Adder #(.width(32)) adder_3 (
    .a(\n32x4乘法器_1_p_31_0 ), .b(shifter_2_out), .out(adder_3_out), .cout(adder_3_cout));  // open: cin
  Adder #(.width(32)) adder_4 (.a(shifter_3_out), .b(bit_extender_3_out), .out(adder_4_out));  // open: cin, cout
  Shifter #(.width(32), .shift("ll")) shifter_3 (.in(\n32x4乘法器_3_p_63_32 ), .\dist (5'b01000), .out(shifter_3_out));
  \_32X4乘法器  \u_32x4乘法器_3  (
    .a_3_0(in_1[11:8]), .b_31_0(in_2), .p_31_0(\n32x4乘法器_3_p_31_0 ), .p_63_32(\n32x4乘法器_3_p_63_32 ));
  assign bit_extender_2_out = {{31{1'b0}}, adder_3_cout};  // Bit_Extender bit_extender_2
  Adder #(.width(32)) adder_5 (.a(adder_2_out), .b(adder_4_out), .out(adder_5_out));  // open: cin, cout
  assign bit_extender_3_out = {{24{1'b0}}, \n32x4乘法器_3_p_31_0 [31:24]};  // Bit_Extender bit_extender_3
  Shifter #(.width(32), .shift("ll")) shifter_4 (.in(\n32x4乘法器_3_p_31_0 ), .\dist (5'b01000), .out(shifter_4_out));
  Adder #(.width(32)) adder_6 (
    .a(adder_3_out), .b(shifter_4_out), .out(adder_6_out), .cout(adder_6_cout));  // open: cin
  Adder #(.width(32)) adder_7 (.a(shifter_5_out), .b(bit_extender_5_out), .out(adder_7_out));  // open: cin, cout
  Shifter #(.width(32), .shift("ll")) shifter_5 (.in(\n32x4乘法器_4_p_63_32 ), .\dist (5'b01100), .out(shifter_5_out));
  Shifter #(.width(32), .shift("ll")) shifter_6 (.in(\n32x4乘法器_4_p_31_0 ), .\dist (5'b01100), .out(shifter_6_out));
  \_32X4乘法器  \u_32x4乘法器_4  (
    .a_3_0(in_1[15:12]), .b_31_0(in_2), .p_31_0(\n32x4乘法器_4_p_31_0 ), .p_63_32(\n32x4乘法器_4_p_63_32 ));
  assign bit_extender_4_out = {{31{1'b0}}, adder_6_cout};  // Bit_Extender bit_extender_4
  Adder #(.width(32)) adder_8 (.a(adder_5_out), .b(adder_7_out), .out(adder_8_out));  // open: cin, cout
  assign bit_extender_5_out = {{20{1'b0}}, \n32x4乘法器_4_p_31_0 [31:20]};  // Bit_Extender bit_extender_5
  Adder #(.width(32)) adder_9 (.a(bit_extender_2_out), .b(bit_extender_4_out), .out(adder_9_out));  // open: cin, cout
  Adder #(.width(32)) adder_10 (
    .a(adder_6_out), .b(shifter_6_out), .out(adder_10_out), .cout(adder_10_cout));  // open: cin
  Adder #(.width(32)) adder_11 (.a(shifter_7_out), .b(bit_extender_7_out), .out(adder_11_out));  // open: cin, cout
  Shifter #(.width(32), .shift("ll")) shifter_7 (.in(\n32x4乘法器_5_p_63_32 ), .\dist (5'b10000), .out(shifter_7_out));
  Shifter #(.width(32), .shift("ll")) shifter_8 (.in(\n32x4乘法器_5_p_31_0 ), .\dist (5'b10000), .out(shifter_8_out));
  \_32X4乘法器  \u_32x4乘法器_5  (
    .a_3_0(in_1[19:16]), .b_31_0(in_2), .p_31_0(\n32x4乘法器_5_p_31_0 ), .p_63_32(\n32x4乘法器_5_p_63_32 ));
  assign bit_extender_6_out = {{31{1'b0}}, adder_10_cout};  // Bit_Extender bit_extender_6
  Adder #(.width(32)) adder_12 (.a(adder_8_out), .b(adder_11_out), .out(adder_12_out));  // open: cin, cout
  assign bit_extender_7_out = {{16{1'b0}}, \n32x4乘法器_5_p_31_0 [31:16]};  // Bit_Extender bit_extender_7
  \_32X4乘法器  \u_32x4乘法器_6  (
    .a_3_0(in_1[23:20]), .b_31_0(in_2), .p_31_0(\n32x4乘法器_6_p_31_0 ), .p_63_32(\n32x4乘法器_6_p_63_32 ));
  Adder #(.width(32)) adder_13 (.a(adder_9_out), .b(bit_extender_6_out), .out(adder_13_out));  // open: cin, cout
  Adder #(.width(32)) adder_14 (
    .a(adder_10_out), .b(shifter_8_out), .out(adder_14_out), .cout(adder_14_cout));  // open: cin
  Adder #(.width(32)) adder_15 (.a(shifter_9_out), .b(bit_extender_8_out), .out(adder_15_out));  // open: cin, cout
  Shifter #(.width(32), .shift("ll")) shifter_9 (.in(\n32x4乘法器_6_p_63_32 ), .\dist (5'b10100), .out(shifter_9_out));
  assign bit_extender_8_out = {{12{1'b0}}, \n32x4乘法器_6_p_31_0 [31:12]};  // Bit_Extender bit_extender_8
  Shifter #(.width(32), .shift("ll")) shifter_10 (.in(\n32x4乘法器_6_p_31_0 ), .\dist (5'b10100), .out(shifter_10_out));
  assign bit_extender_9_out = {{31{1'b0}}, adder_14_cout};  // Bit_Extender bit_extender_9
  Adder #(.width(32)) adder_16 (.a(adder_12_out), .b(adder_15_out), .out(adder_16_out));  // open: cin, cout
  Adder #(.width(32)) adder_17 (
    .a(adder_14_out), .b(shifter_10_out), .out(adder_17_out), .cout(adder_17_cout));  // open: cin
  Shifter #(.width(32), .shift("ll")) shifter_11 (.in(\n32x4乘法器_7_p_63_32 ), .\dist (5'b11000), .out(shifter_11_out));
  \_32X4乘法器  \u_32x4乘法器_7  (
    .a_3_0(in_1[27:24]), .b_31_0(in_2), .p_31_0(\n32x4乘法器_7_p_31_0 ), .p_63_32(\n32x4乘法器_7_p_63_32 ));
  Adder #(.width(32)) adder_18 (.a(adder_13_out), .b(bit_extender_9_out), .out(adder_18_out));  // open: cin, cout
  assign bit_extender_10_out = {{31{1'b0}}, adder_17_cout};  // Bit_Extender bit_extender_10
  Adder #(.width(32)) adder_19 (.a(shifter_11_out), .b(bit_extender_11_out), .out(adder_19_out));  // open: cin, cout
  assign bit_extender_11_out = {{8{1'b0}}, \n32x4乘法器_7_p_31_0 [31:8]};  // Bit_Extender bit_extender_11
  Shifter #(.width(32), .shift("ll")) shifter_12 (.in(\n32x4乘法器_7_p_31_0 ), .\dist (5'b11000), .out(shifter_12_out));
  Adder #(.width(32)) adder_20 (.a(adder_18_out), .b(bit_extender_10_out), .out(adder_20_out));  // open: cin, cout
  Adder #(.width(32)) adder_21 (.a(adder_16_out), .b(adder_19_out), .out(adder_21_out));  // open: cin, cout
  Adder #(.width(32)) adder_22 (
    .a(adder_17_out), .b(shifter_12_out), .out(adder_22_out), .cout(adder_22_cout));  // open: cin
  Shifter #(.width(32), .shift("ll")) shifter_13 (.in(\n32x4乘法器_8_p_63_32 ), .\dist (5'b11100), .out(shifter_13_out));
  \_32X4乘法器  \u_32x4乘法器_8  (
    .a_3_0(in_1[31:28]), .b_31_0(in_2), .p_31_0(\n32x4乘法器_8_p_31_0 ), .p_63_32(\n32x4乘法器_8_p_63_32 ));
  assign bit_extender_12_out = {{31{1'b0}}, adder_22_cout};  // Bit_Extender bit_extender_12
  Adder #(.width(32)) adder_23 (.a(adder_21_out), .b(adder_24_out), .out(adder_23_out));  // open: cin, cout
  Adder #(.width(32)) adder_24 (.a(shifter_13_out), .b(bit_extender_13_out), .out(adder_24_out));  // open: cin, cout
  assign bit_extender_13_out = {{4{1'b0}}, \n32x4乘法器_8_p_31_0 [31:4]};  // Bit_Extender bit_extender_13
  Shifter #(.width(32), .shift("ll")) shifter_14 (.in(\n32x4乘法器_8_p_31_0 ), .\dist (5'b11100), .out(shifter_14_out));
  Adder #(.width(32)) adder_25 (.a(adder_20_out), .b(bit_extender_12_out), .out(adder_25_out));  // open: cin, cout
  Adder #(.width(32)) adder_26 (.a(adder_22_out), .b(shifter_14_out), .out(p_31_0), .cout(adder_26_cout));  // open: cin
  assign bit_extender_14_out = {{31{1'b0}}, adder_26_cout};  // Bit_Extender bit_extender_14
  Adder #(.width(32)) adder_27 (.a(adder_25_out), .b(bit_extender_14_out), .out(adder_27_out));  // open: cin, cout
  Adder #(.width(32)) adder_28 (.a(adder_27_out), .b(adder_23_out), .out(p_63_32));  // open: cin, cout
endmodule

module \_32X32乘法器测试电路  (
  input  [31:0] a_31_0,
  input  [31:0] b_31_0,
  output [31:0] p_63_32,
  output [31:0] p_31_0,
  output [31:0] out_5,
  output [31:0] p_31_0_2,
  output [31:0] p_63_32_2
);

  \_32X32乘法器  \u_32x32乘法器_1  (.in_1(a_31_0), .in_2(b_31_0), .p_63_32(p_63_32), .p_31_0(p_31_0));
  Multiplier #(.width(32)) multiplier_1 (.a(a_31_0), .b(b_31_0), .out(p_31_0_2), .cout(p_63_32_2));  // open: cin
  assign out_5 = p_31_0 ^ p_31_0_2;  // XOR_Gate xor_1, 32 bits wide
endmodule
